# Fritzing sketch kartino (saved by Fritzing 0.8.5b)

parts:
  Componente2 = Triple Axis Accelerometer Breakout - ADXL335
  Componente3 = Arduino Uno (Rev3)

nets:
  N1: Componente2.YOUT, Componente3.A1
  N2: Componente2.XOUT, Componente3.A0
  GND: Componente2.GND, Componente3.GND
  VCC: Componente2.VCC, Componente3.3V3
